// Logisim project Computador simulador.circ as structural Verilog
module main (
  input  CLEAR,
  output [4:0] out_2,
  output [1:0] out_3,
  output [1:0] out_4,
  output [3:0] out_5,
  output [1:0] out_6,
  output [4:0] out_7,
  output [7:0] out_8,
  output [7:0] out_9,
  output [7:0] out_10,
  output [7:0] out_11,
  output [7:0] out_12,
  output [7:0] out_13,
  output [7:0] out_14,
  output [7:0] out_15
);

  wire ADD, bitselector_1_out, CLK, clock_1_out, controlled_buffer_2_out, EQ, GEQ, GT, HLT, JMP, LEQ, LT,
       MovRxRA, MovRxRy, MUL, not_1_out, not_2_out, RDM, STR, SUB;
  wire [7:0] controlled_buffer_3_out, Saida_ROM;

  Clock clock_1 (.out(clock_1_out));
  assign CLK = not_1_out ? clock_1_out : 1'bz;  // Controlled_Buffer controlled_buffer_1
  not not_1 (not_1_out, HLT);
  \Decode_instruções  \decode_instruções_1  (
    .Operacao(out_5), .EQ(EQ), .LT(LT), .GT(GT), .LEQ(LEQ), .GEQ(GEQ), .JMP(JMP), .MUL(MUL), .ADD(ADD),
    .SUB(SUB), .MovRxRy(MovRxRy), .MovRxRA(MovRxRA), .RDM(RDM), .STR(STR), .HLT(HLT));
  BitSelector bitselector_1 (.in(out_9), .out(bitselector_1_out), .sel(3'b000));
  assign controlled_buffer_2_out = bitselector_1_out ? JMP : 1'bz;  // Controlled_Buffer controlled_buffer_2
  not not_2 (not_2_out, controlled_buffer_2_out);
  PC pc_1 (
    .CONTADOR(out_7), .CLK(CLK), .reset(CLEAR), .Load(controlled_buffer_2_out), .Count(not_2_out),
    .\input (out_2));
  assign controlled_buffer_3_out = RDM ? out_8 : 8'bz;  // Controlled_Buffer controlled_buffer_3
  assign controlled_buffer_3_out = MovRxRA ? out_9 : 8'bz;  // Controlled_Buffer controlled_buffer_4
  assign controlled_buffer_3_out = MovRxRy ? out_10 : 8'bz;  // Controlled_Buffer controlled_buffer_5
  \Registrador_de_instrução  \registrador_de_instrução_1  (
    .Instrucao_ROM(Saida_ROM), .Ry(out_3), .Rx(out_4), .\Instrução_decodificador (out_5), .CLK(CLK),
    .clear(CLEAR));
  Register #(.trigger("falling")) RA (.D(out_13), .Q(out_9), .clk(CLK), .clr(CLEAR));  // open: en
  Banco_de_registradores banco_de_registradores_1 (
    .RX(out_4), .CLK(CLK), .Conteudo_RX({out_11[7:5], out_2}), .Conteudo_Ry(out_10), .Rx_2(out_4),
    .Ry(out_3), .reset(CLEAR), .Input_banco(controlled_buffer_3_out));
  assign out_6 = RDM ? out_3 : 2'bz;  // Controlled_Buffer controlled_buffer_6
  assign out_6 = STR ? out_4 : 2'bz;  // Controlled_Buffer controlled_buffer_7
  ROM #(.addrWidth(5)) rom_1 (.addr(out_7), .data(Saida_ROM));  // open: sel
  RAM #(.addrWidth(2), .bus("separate")) ram_1 (
    .addr(out_6), .din(out_10), .data(out_8), .str(STR), .clk(CLK), .ld(RDM));  // open: sel, clr
  ULA ula_1 (
    .Entrada_Rx({out_11[7:5], out_2}), .Entrada_Ry(out_10), .ADD(ADD), .SUB(SUB), .MUL(MUL), .EQ(EQ),
    .LT(LT), .GT(GT), .GEQ(GEQ), .LEQ(LEQ), .ACULUMADOR(out_13));

  assign out_11[4:0] = out_2;
  assign out_12 = {out_11[7:5], out_2};
  assign out_14 = out_10;
  assign out_15 = out_10;

  // Other names for the same wires on the sheet: Acumulador[7:0] = out_13; CONTADOR[4:0] = out_7;
  //   ConteudoRX[7:0] = {out_11[7:5], out_2}; desvio[4:0] = out_2; Input_RAMRx[7:0] = {out_11[7:5], out_2};
  //   ConteudoRY[7:0] = out_10; Input_RAMRy[7:0] = out_10; OPERACAO[3:0] = out_5; RA[7:0] = out_9; RAM[7:0] = out_8;
  //   Rx[1:0] = out_4; Ry[1:0] = out_3

  // Notes on the sheet:
  //   DECODIFICADOR DE INSTRUÇÕES 
  //   CONTADOR DE PROGRAMA
  //   RDM Rx , End; [Rx] ← End. mem dados
  //   MOV Rx , RA	;        [Rx] ← [RA]
  //   MOV Rx , Ry	;        [Rx] ← [Ry]
  //   Registrador de Instrução 
  //   END RAM
  //   END REGISTRADOR
  //   REGISTRADOR ACUMULADOR
  //   BANCO DE REGISTRADORES
  //   Memoria de programa
  //   Memoria Dados
  //   contents of rom_1 (hex, n*v repeats v):
  //   d0 d5 df 9b c8 ee a1 c0 2b d6 74 bb d5 61 74 f0 c9 d5 61 74 f0
  //   INSTRUÇÃO
  //   ULA
endmodule

module ULA (
  input  EQ,
  input  [7:0] Entrada_Rx,
  input  LT,
  input  [7:0] Entrada_Ry,
  input  GT,
  input  LEQ,
  input  GEQ,
  input  ADD,
  input  SUB,
  input  MUL,
  output [7:0] ACULUMADOR
);

  wire comparator_1_eq, comparator_2_lt, comparator_3_eq, comparator_3_lt, comparator_4_eq, comparator_4_gt,
       comparator_5_gt, controlled_buffer_4_out, or_1_out, or_2_out, or_3_out, or_4_out;
  wire [7:0] adder_1_out, multiplier_1_out, OutCOMP, OutOP, subtractor_1_out;

  Comparator comparator_1 (.a(Entrada_Rx), .b(Entrada_Ry), .eq(comparator_1_eq));  // open: gt, lt
  Comparator comparator_2 (.a(Entrada_Rx), .b(Entrada_Ry), .lt(comparator_2_lt));  // open: gt, eq
  Comparator comparator_3 (.a(Entrada_Rx), .b(Entrada_Ry), .eq(comparator_3_eq), .lt(comparator_3_lt));  // open: gt
  Comparator comparator_4 (.a(Entrada_Rx), .b(Entrada_Ry), .gt(comparator_4_gt), .eq(comparator_4_eq));  // open: lt
  Comparator comparator_5 (.a(Entrada_Rx), .b(Entrada_Ry), .gt(comparator_5_gt));  // open: eq, lt
  or or_1 (or_1_out, comparator_3_eq, comparator_3_lt);
  or or_2 (or_2_out, comparator_4_gt, comparator_4_eq);
  Adder adder_1 (.a(Entrada_Rx), .b(Entrada_Ry), .out(adder_1_out));  // open: cin, cout
  assign OutOP = ADD ? adder_1_out : 8'bz;  // Controlled_Buffer controlled_buffer_1
  assign OutOP = SUB ? subtractor_1_out : 8'bz;  // Controlled_Buffer controlled_buffer_2
  Subtractor subtractor_1 (.a(Entrada_Rx), .b(Entrada_Ry), .out(subtractor_1_out));  // open: bin, bout
  assign OutOP = MUL ? multiplier_1_out : 8'bz;  // Controlled_Buffer controlled_buffer_3
  Multiplier multiplier_1 (.a(Entrada_Rx), .b(Entrada_Ry), .out(multiplier_1_out));  // open: cin, cout
  assign controlled_buffer_4_out = EQ ? comparator_1_eq : 1'bz;  // Controlled_Buffer controlled_buffer_4
  assign controlled_buffer_4_out = LT ? comparator_2_lt : 1'bz;  // Controlled_Buffer controlled_buffer_5
  assign controlled_buffer_4_out = GT ? comparator_5_gt : 1'bz;  // Controlled_Buffer controlled_buffer_6
  assign controlled_buffer_4_out = LEQ ? or_1_out : 1'bz;  // Controlled_Buffer controlled_buffer_7
  assign controlled_buffer_4_out = GEQ ? or_2_out : 1'bz;  // Controlled_Buffer controlled_buffer_8
  assign OutCOMP = {{7{1'b0}}, controlled_buffer_4_out};  // Bit_Extender bit_extender_1
  or or_3 (or_3_out, EQ, LT, GT, LEQ, GEQ);
  assign ACULUMADOR = or_3_out ? OutCOMP : 8'bz;  // Controlled_Buffer controlled_buffer_9
  or or_4 (or_4_out, ADD, SUB, MUL);
  assign ACULUMADOR = or_4_out ? OutOP : 8'bz;  // Controlled_Buffer controlled_buffer_10

  // Other names for the same wires on the sheet: SaidaRx[7:0] = Entrada_Rx; SaidaRy[7:0] = Entrada_Ry
endmodule

module PC (
  input  Load,
  input  [4:0] \input ,
  input  reset,
  input  CLK,
  input  Count,
  output [4:0] CONTADOR
);

  Counter #(.width(5), .max('h1f), .trigger("falling")) counter_1 (
    .load(Load), .D(\input ), .count(Count), .Q(CONTADOR), .clk(CLK), .clr(reset));  // open: carry
endmodule

module \Registrador_de_instrução  (
  input  [7:0] Instrucao_ROM,
  input  CLK,
  input  clear,
  output [1:0] Ry,
  output [1:0] Rx,
  output [3:0] \Instrução_decodificador 
);

  Register register_1 (.D(Instrucao_ROM), .Q({\Instrução_decodificador , Rx, Ry}), .clk(CLK), .clr(clear));  // open: en

  // Notes on the sheet:
  //   Ex:
  //   ADD RX, RY
  //   Bits mais significativos são da INSTRUÇÃO; do meio Rx, ultimos dois bits Ry
  //   01
  //   1001
  //   end Ram
  //   10
  //   end registrador
endmodule

module Banco_de_registradores (
  input  [1:0] RX,
  input  [1:0] Rx_2,
  input  [7:0] Input_banco,
  input  [1:0] Ry,
  input  CLK,
  input  reset,
  output [7:0] Conteudo_RX,
  output [7:0] Conteudo_Ry
);

  wire R0, R1, R2, R3;
  wire [7:0] Out_R0, Out_R1, Out_R2, Out_R3;

  Decoder #(.select(2)) decoder_1 (.out0(R0), .out1(R1), .out2(R2), .out3(R3), .sel(RX));  // open: en
  Register #(.trigger("falling")) u_R0 (.D(Input_banco), .en(R0), .Q(Out_R0), .clk(CLK), .clr(reset));
  Register #(.trigger("falling")) u_R1 (.D(Input_banco), .en(R1), .Q(Out_R1), .clk(CLK), .clr(reset));
  Register #(.trigger("falling")) u_R2 (.D(Input_banco), .en(R2), .Q(Out_R2), .clk(CLK), .clr(reset));
  Register #(.trigger("falling")) u_R3 (.D(Input_banco), .en(R3), .Q(Out_R3), .clk(CLK), .clr(reset));
  Multiplexer #(.select(2), .width(8)) multiplexer_1 (
    .in0(Out_R0), .in1(Out_R1), .in2(Out_R2), .in3(Out_R3), .out(Conteudo_RX), .sel(Rx_2));  // open: en
  Multiplexer #(.select(2), .width(8)) multiplexer_2 (
    .in0(Out_R0), .in1(Out_R1), .in2(Out_R2), .in3(Out_R3), .out(Conteudo_Ry), .sel(Ry));  // open: en

  // Other names for the same wires on the sheet: clear = reset

  // Notes on the sheet:
  //   End RAM
  //   iDENTIFICAÇÃO DO REGISTRADOR
  //   REGISTRADORES
  //   SAÍDAS QUE VAO PRA ULA
endmodule

module \Decode_instruções  (
  input  [3:0] Operacao,
  output EQ,
  output LT,
  output GT,
  output LEQ,
  output GEQ,
  output JMP,
  output MUL,
  output ADD,
  output SUB,
  output MovRxRy,
  output MovRxRA,
  output RDM,
  output STR,
  output HLT
);

  Comparator #(.width(4)) comparator_1 (.a(Operacao), .b(4'b0010), .eq(EQ));  // open: gt, lt
  Comparator #(.width(4)) comparator_2 (.a(Operacao), .b(4'b0011), .eq(LT));  // open: gt, lt
  Comparator #(.width(4)) comparator_3 (.a(Operacao), .b(4'b0100), .eq(GT));  // open: gt, lt
  Comparator #(.width(4)) comparator_4 (.a(Operacao), .b(4'b0101), .eq(LEQ));  // open: gt, lt
  Comparator #(.width(4)) comparator_5 (.a(Operacao), .b(4'b0110), .eq(GEQ));  // open: gt, lt
  Comparator #(.width(4)) comparator_6 (.a(Operacao), .b(4'b0111), .eq(JMP));  // open: gt, lt
  Comparator #(.width(4)) comparator_7 (.a(Operacao), .b(4'b1000), .eq(MUL));  // open: gt, lt
  Comparator #(.width(4)) comparator_8 (.a(Operacao), .b(4'b1001), .eq(ADD));  // open: gt, lt
  Comparator #(.width(4)) comparator_9 (.a(Operacao), .b(4'b1010), .eq(SUB));  // open: gt, lt
  Comparator #(.width(4)) comparator_10 (.a(Operacao), .b(4'b1011), .eq(MovRxRy));  // open: gt, lt
  Comparator #(.width(4)) comparator_11 (.a(Operacao), .b(4'b1100), .eq(MovRxRA));  // open: gt, lt
  Comparator #(.width(4)) comparator_12 (.a(Operacao), .b(4'b1101), .eq(RDM));  // open: gt, lt
  Comparator #(.width(4)) comparator_13 (.a(Operacao), .b(4'b1110), .eq(STR));  // open: gt, lt
  Comparator #(.width(4)) comparator_14 (.a(Operacao), .b(4'b1111), .eq(HLT));  // open: gt, lt
endmodule

module ula (
  input  [7:0] Operando_1,
  input  [7:0] Operando_2,
  input  [3:0] Seletor,
  output [7:0] \Saída 
);

  wire comparator_1_eq, comparator_2_eq, comparator_3_lt, comparator_4_eq, comparator_4_lt, or_2_out;
  wire [7:0] adder_1_out, and_1_out, bit_extender_1_out, bit_extender_2_out, bit_extender_3_out,
       bit_extender_4_out, divider_1_out, multiplier_1_out, or_1_out, subtractor_1_out;

  assign and_1_out = Operando_1 & Operando_2;  // AND_Gate and_1, 8 bits wide
  assign or_1_out = Operando_1 | Operando_2;  // OR_Gate or_1, 8 bits wide
  Comparator comparator_1 (.a(Operando_1), .b({8{1'b0}}), .eq(comparator_1_eq));  // open: gt, lt
  Adder adder_1 (.a(Operando_1), .b(Operando_2), .out(adder_1_out));  // open: cin, cout
  Subtractor subtractor_1 (.a(Operando_1), .b(Operando_2), .out(subtractor_1_out));  // open: bin, bout
  Multiplier multiplier_1 (.a(Operando_1), .b(Operando_2), .out(multiplier_1_out));  // open: cin, cout
  Divider divider_1 (.a(Operando_1), .b(Operando_2), .out(divider_1_out));  // open: upper, rem
  Comparator comparator_2 (.a(Operando_1), .b(Operando_2), .eq(comparator_2_eq));  // open: gt, lt
  Comparator comparator_3 (.a(Operando_1), .b(Operando_2), .lt(comparator_3_lt));  // open: gt, eq
  Comparator comparator_4 (.a(Operando_1), .b(Operando_2), .eq(comparator_4_eq), .lt(comparator_4_lt));  // open: gt
  assign bit_extender_1_out = {{7{1'b0}}, comparator_1_eq};  // Bit_Extender bit_extender_1
  assign bit_extender_2_out = {{7{1'b0}}, comparator_2_eq};  // Bit_Extender bit_extender_2
  assign bit_extender_3_out = {{7{1'b0}}, comparator_3_lt};  // Bit_Extender bit_extender_3
  assign bit_extender_4_out = {{7{1'b0}}, or_2_out};  // Bit_Extender bit_extender_4
  or or_2 (or_2_out, comparator_4_eq, comparator_4_lt);
  Multiplexer #(.select(4), .width(8), .enable("false")) multiplexer_1 (
    .in0(and_1_out), .in1(or_1_out), .in2(bit_extender_1_out), .in3(adder_1_out), .in4(subtractor_1_out),
    .in5(multiplier_1_out), .in6(divider_1_out), .in7(bit_extender_2_out), .in8(bit_extender_3_out),
    .in9(bit_extender_4_out), .out(\Saída ), .sel(Seletor));  // open: in10, in11, in12, in13, in14, in15
endmodule
